# Fritzing sketch SPI_OLED_NANO_battery_SOC_meter_fritzing (saved by Fritzing 0.9.3b)
breadboards: 1

parts:
  Part1 = Arduino Nano (Rev3.0)
  Low = Trimmer Potentiometer [maximum_resistance=10kΩ package=THT]  # not connected
  High = Trimmer Potentiometer [maximum_resistance=10kΩ package=THT]  # not connected
  VCC1 = Battery
  shunt = Resistor [tolerance=±5% resistance=1 package=THT]
  K1 = Relay [part_number=FRS1B-S package=THT]
  Charger = Power plug
  LED1 = LED - 5mm [color="Red (633nm)" package="5 mm [THT]"]
  R3 = Resistor [tolerance=±5% resistance=220 package=THT]
  electronicsguy1 = electronicsguy 0.96" 128x64 SPI I2C OLED

nets:
  GND: Part1.GND, VCC1.-, Charger.GND, R3.Pin_1, electronicsguy1.GND
  N1: Part1.D2, K1.COIL1
  N2: Part1.D8, electronicsguy1.RST
  N3: Part1.D9, electronicsguy1.DC
  N4: Part1.D10, electronicsguy1.CS
  N5: Part1.D11/MOSI, electronicsguy1.D1
  N6: Part1.A1, shunt.Pin_1, K1.C2
  N7: Part1.A0, VCC1.+, shunt.Pin_0
  3V3: Part1.3V3, electronicsguy1.VCC
  N8: Part1.D13/SCK, electronicsguy1.D0
  N9: K1.A, LED1.cathode
  N10: K1.B, Charger.VCC
  N11: LED1.anode, R3.Pin_0

custom parts:
  electronicsguy 0.96" 128x64 SPI I2C OLED: Generic 0.96" 128x64 SPI I2C OLED Default is SPI mode Can be re-configured for I2C (needs soldering work) Comes in various colors like blue, white, yellow-blue
